# Fritzing sketch SmartRoomController (saved by Fritzing 0.9.4)
breadboards: 3

parts:
  Breadboard4 = Breadboard Split Power
  Breadboard5 = Breadboard Split Power
  Ethernet = WIZ820io [part_number=WIZ820io]
  S1 = Pushbutton [package="[THT]"]
  Buzzer = KY-006 Passive Buzzer Module [package="Breakout board"]
  DHT11 = KY-015 Temperature & Humidity Sensor Module [package="Breakout board"]
  R1 = Resistor [tolerance=±5% resistance=220 package="0603 [SMD]"]
  Teensy_3_2 = Teensy 3.1

nets:
  N1: Breadboard4.pin15Y, Breadboard4.pin17Y, Breadboard4.pin29Y, Breadboard5.pin3Y, Breadboard5.pin15Y, Breadboard5.pin17Y
  N2: Breadboard4.pin29Z, Breadboard5.pin3Z
  GND: Ethernet.GND, Buzzer.-, DHT11.-, R1.Pin_1, Teensy_3_2.GND
  N3: Ethernet.MOSI, Teensy_3_2.D11
  N4: Ethernet.SCLK, Teensy_3_2.D13
  N5: Ethernet.nSS, Teensy_3_2.D10
  N6: Ethernet.MISO, Teensy_3_2.D12
  N7: Ethernet.nRESET, Teensy_3_2.A9/D23
  VIN: Ethernet.VIN, S1.Pin_1, S1.Pin_2, DHT11.Vin, R1.Pin_0, Teensy_3_2.3V3
  N8: S1.Pin_3, S1.Pin_4, Teensy_3_2.A8/D22
  N9: Buzzer.S, Teensy_3_2.A1/D15
  N10: DHT11.S, Teensy_3_2.A0/D14

custom parts:
  Breadboard Split Power: A custom 6 pin per group power supply strip where the top row (ground) is all bussed together and the bottom row (+V) is split in two groups of 12 pins. This version is modified to be a loadable part and was rescaled to be on the standard 1px = 1thou grid with the size set in inches
  Pushbutton: A generic pushbutton.
  KY-006 Passive Buzzer Module: Passive Piezoelectric Buzzer Module Keyes KY-006, it can produce a range of sound tones depending on the input frequency.
  KY-015 Temperature & Humidity Sensor Module: KY-015 temperature and humidity sensor module, provides a low-latency serial interface to measure humidity and temperature.
